# Fritzing sketch Esquema Micros Practica #5a rep (saved by Fritzing 0.9.3b)
breadboards: 3

parts:
  Part1 = Arduino Mega 2560 (Rev3) [part_number=8088]
  IC1 = IC, DIP package, 20 pins [chip_label="74LS373 Latch" part_number="LATCH 74LS373"]
  IC3 = IC, DIP package, 20 pins [chip_label="74LS373 Latch" part_number="LATCH 74LS373"]
  IC4 = IC, DIP package, 14 pins [chip_label=IC part_number=7404]
  IC5 = IC, DIP package, 14 pins [chip_label=IC part_number=7408]
  IC6 = IC, DIP package, 14 pins [chip_label=IC part_number=7408]
  IC7_7400 = IC, DIP package, 14 pins [chip_label=IC part_number=7400]
  IC9 = IC, DIP package, 14 pins [chip_label=IC part_number=7432]

nets:
  N1: Part1.GND, IC1.pin10, IC4.pin7, IC5.pin7, IC6.pin7, IC7_7400.pin7, IC9.pin7
  N2: Part1.IOREF, IC3.pin20
  N3: Part1.5V, IC1.pin20
  D0: Part1.AD0, IC1.pin3, IC3.pin3
  D1: Part1.AD1, IC1.pin4, IC3.pin4
  D2: Part1.AD2, IC1.pin7, IC3.pin7
  D3: Part1.AD3, IC1.pin8, IC3.pin8
  D4: Part1.AD4, IC1.pin13, IC3.pin13
  D5: Part1.AD5, IC1.pin14, IC3.pin14
  D6: Part1.AD6, IC1.pin17, IC3.pin17
  D7: Part1.AD7, IC1.pin18, IC3.pin18
  N4: Part1.A15, IC5.pin1
  N5: Part1.A14, IC5.pin2
  N6: Part1.A13, IC5.pin4
  N7: Part1.A12, IC5.pin5
  N8: Part1.A11, IC5.pin13
  N9: Part1.A10, IC5.pin12
  N10: Part1.A9, IC5.pin10
  N11: Part1.A8, IC5.pin9
  ALE: Part1.ALE, IC1.pin11
  WR: Part1./WR, IC4.pin1
  N12: IC1.pin2, IC6.pin1
  N13: IC1.pin5, IC6.pin2
  N14: IC1.pin6, IC6.pin4
  N15: IC1.pin9, IC6.pin5
  N16: IC1.pin12, IC6.pin13
  N17: IC1.pin15, IC6.pin12
  N18: IC1.pin16, IC6.pin10
  N19: IC1.pin19, IC6.pin9
  LE: IC3.pin11, IC9.pin8
  N20: IC4.pin2, IC9.pin9
  N21: IC5.pin3, IC7_7400.pin13
  N22: IC5.pin6, IC7_7400.pin12
  N23: IC5.pin8, IC7_7400.pin9
  N24: IC5.pin11, IC7_7400.pin10
  N25: IC6.pin3, IC7_7400.pin1
  N26: IC6.pin6, IC7_7400.pin2
  N27: IC6.pin8, IC7_7400.pin5
  N28: IC6.pin11, IC7_7400.pin4
  N29: IC7_7400.pin3, IC9.pin1
  N30: IC7_7400.pin6, IC9.pin2
  N31: IC7_7400.pin8, IC9.pin12
  N32: IC7_7400.pin11, IC9.pin13
  N33: IC9.pin3, IC9.pin4
  N34: IC9.pin5, IC9.pin11
  N35: IC9.pin6, IC9.pin10

custom parts:
  Arduino Mega 2560 (Rev3): The Arduino Mega 2560 is a microcontroller board based on the ATmega2560 (datasheet). It has 54 digital input/output pins (of which 14 can be used as PWM outputs), 16 analog inputs, 4 UARTs (hardware serial ports), a 16 MHz crystal oscillator, a USB connection, a power jack, an ICSP header, and a reset button. It contains everything needed to support the microcontroller; simply connect it to a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
