# Fritzing sketch Practica3 Micros (saved by Fritzing 0.9.3b)
breadboards: 1

parts:
  8088 = Arduino Mega 2560 (Rev3)
  IC1 = IC, DIP package, 20 pins [chip_label="Latch 373"]
  IC2 = IC, DIP package, 28 pins [chip_label="Memoria RAM 256"]

nets:
  N1: 8088.5V, IC1.pin20, IC2.pin28
  N2: 8088.D22, IC1.pin3
  N3: 8088.D23, IC1.pin4
  N4: 8088.D24, IC1.pin7
  N5: 8088.D25, IC1.pin8
  N6: 8088.D26, IC1.pin13
  N7: 8088.D27, IC1.pin14, IC2.pin17
  N8: 8088.D28, IC1.pin17, IC2.pin18
  N9: 8088.D29, IC1.pin18, IC2.pin19
  A14: 8088.D31, IC2.pin1
  A13: 8088.D32, IC2.pin26
  A12: 8088.D33, IC2.pin2
  A11: 8088.D34, IC2.pin23
  A10: 8088.D35, IC2.pin21
  A9: 8088.D36, IC2.pin24
  A8: 8088.D37, IC2.pin25
  ALE: 8088.D39, IC1.pin11
  /READ: 8088.D40, IC2.pin22
  /WE: 8088.D41, IC2.pin27
  GND: 8088.GND, IC1.pin1, IC1.pin10, IC2.pin20
  Q7: IC2.pin3
